# Fritzing sketch mculed (saved by Fritzing 0.9.3b)
circuit board: 8.46667cm x 5.64444cm
breadboards: 1

parts:
  Part3 = Logic Level Converter
  Q1 = Basic FET N-Channel [part_number=FQP30N06L package="TO220 [THT]"]
  S1 = Momentary Switch [part_number="Local Control" package=ksa_sealed_tac_switch]
  JP1 = Header 5 [part_number="LED Strip" package=1x05-1mm-ra]
  M1 = RioRand LM2596
  Power_plug1 = Power plug
  U1 = NodeMCU V1.0

nets:
  N1: Part3.TX2_LV, U1.D5
  GND: Part3.GND, Q1.source, S1.1, S1.2, JP1.5, M1.Pin_2, M1.Pin_4, Power_plug1.GND, U1.GND
  N2: Part3.LV, U1.3V3
  N3: Part3.TX_LV, U1.D4
  N4: Part3.TX_HV, JP1.2
  N5: Part3.HV, M1.Pin_3, U1.Vin
  N6: Part3.TX2_HV, Q1.gate
  N7: Q1.drain, JP1.4
  N8: S1.3, S1.4, U1.D1
  N9: JP1.1, M1.Pin_1, Power_plug1.VCC

notes:
  homebridge-mculed, ESP8266/RGB+W/WS2812 LED Strip controller, 1.0
  LED Strip Connector
  1 - 24V - Black
  2 - DIN - Red
  3 - Check - Green
  4 - W - Yellow
  5 - Gnd - Blue

custom parts:
  NodeMCU V1.0: ESP8266 based NodeMCU
